// Logisim project cpu.circ as structural Verilog: 5 circuits, main circuit main
module main (
  input  [31:0] INSTRUCTION,
  input  CLOCK,
  output [31:0] PROGRAM_COUNTER,
  output [31:0] ra,
  output [31:0] sp,
  output [31:0] t0,
  output [31:0] t1,
  output [31:0] t2,
  output [31:0] s0,
  output [31:0] s1,
  output [31:0] a0
);

  wire ASel, BrEq, BrLT, BrUn, BSel, MemRW, PCSel, RegWEn;
  wire [1:0] WBSel;
  wire [2:0] ImmSel;
  wire [3:0] ALUSel;
  wire [4:0] rd, rs1, rs2;
  wire [31:0] ALUOut, imm, instID, MemData, multiplexer_1_out, multiplexer_2_out, multiplexer_3_out, PCPlus4,
       rs1Out, rs2Out, wb;

  Adder #(.width(32)) adder_1 (.a(PROGRAM_COUNTER), .b(32'h4), .out(PCPlus4));  // open: cin, cout
  Register #(.width(32)) register_1 (.D(INSTRUCTION), .clk(CLOCK), .Q(instID));  // open: en, clr
  Multiplexer #(.width(32), .enable("false")) multiplexer_1 (
    .in0(PCPlus4), .in1(ALUOut), .out(multiplexer_1_out), .sel(PCSel));
  Register #(.width(32)) PC (.D(multiplexer_1_out), .clk(CLOCK), .Q(PROGRAM_COUNTER));  // open: en, clr
  Decodery decodery_1 (
    .Instruction(instID), .rd(rd), .rs1(rs1), .rs2(rs2));  // open: opcode, funct3, funct7, immI, immS, immB, immU, immJ
  ImmGen immgen_1 (.Instruction(instID), .ImmSel(ImmSel), .clk(CLOCK), .imm(imm));
  regfile_main RegFile (
    .rs2(rs2), .rd(rd), .Read_Data_1(rs1Out), .Read_Data_2(rs2Out), .ra(ra), .sp(sp), .t0(t0), .t1(t1),
    .t2(t2), .s0(s0), .s1(s1), .a0(a0), .rs1(rs1), .Write_Data(wb), .RegWEn(RegWEn), .clk(CLOCK));
  BrCmp brcmp_1 (.rs1(rs1Out), .rs2(rs2Out), .BrUn(BrUn), .BrEq(BrEq), .BrLt(BrLT));
  Control control_1 (
    .Instruction(INSTRUCTION), .BrEq(BrEq), .BrLt(BrLT), .PCSel(PCSel), .RegWEn(RegWEn), .ImmSel(ImmSel),
    .BrUn(BrUn), .BSel(BSel), .ASel(ASel), .ALUSel(ALUSel), .MemRW(MemRW), .WBSel(WBSel));
  Multiplexer #(.width(32), .enable("false")) multiplexer_2 (
    .in0(rs1Out), .in1(PROGRAM_COUNTER), .out(multiplexer_2_out), .sel(ASel));
  Multiplexer #(.width(32), .enable("false")) multiplexer_3 (
    .in0(rs2Out), .in1(imm), .out(multiplexer_3_out), .sel(BSel));
  alu alu_1 (.B(multiplexer_3_out), .Result(ALUOut), .A(multiplexer_2_out), .ALUSel(ALUSel));
  // mem_main main_1: pin names not known; wires that end beside it: ALUOut, rs2Out, CLOCK, MemRW, MemData
  Multiplexer #(.select(2), .width(32), .enable("false")) multiplexer_4 (
    .in0(PCPlus4), .in1(ALUOut), .in2(MemData), .out(wb), .sel(WBSel));  // open: in3
  // also tied to GND on the sheet: {ASel, ImmSel[0], ImmSel[1], ImmSel[2], PCSel, WBSel[1]}
  // also tied to VCC on the sheet: {BSel, RegWEn, WBSel[0]}

  // Other names for the same wires on the sheet: clk = CLOCK

  // Notes on the sheet:
  //   Output
  //   IMEM (do **NOT** move this)
  //   Inputs
  //   Inputs/Outputs for testing. Do **NOT** move these.
endmodule

module ImmGen (
  input  [31:0] Instruction,
  input  [2:0] ImmSel,
  input  clk,
  output [31:0] imm
);

  wire bitselector_1_out, bitselector_2_out, bitselector_3_out, bitselector_4_out;
  wire [11:0] immI, immS;
  wire [12:0] immB;
  wire [20:0] immJ;
  wire [31:0] and_1_out, and_2_out, and_3_out, and_4_out, B, bit_extender_1_out, bit_extender_2_out,
       bit_extender_3_out, bit_extender_4_out, I, immU, J, S;

  Decodery decodery_1 (
    .Instruction(Instruction), .immI(immI), .immS(immS), .immB(immB), .immU(immU), .immJ(immJ));  // open: opcode, rd, rs1, rs2, funct3, funct7
  BitSelector #(.width(12)) bitselector_1 (.in(immI), .out(bitselector_1_out), .sel(4'b1011));
  BitSelector #(.width(12)) bitselector_2 (.in(immS), .out(bitselector_2_out), .sel(4'b1011));
  BitSelector #(.width(13)) bitselector_3 (.in(immB), .out(bitselector_3_out), .sel(4'b1101));
  BitSelector #(.width(21)) bitselector_4 (.in(immJ), .out(bitselector_4_out), .sel(5'b10101));
  assign bit_extender_1_out = {{20{immI[11]}}, immI};  // Bit_Extender bit_extender_1
  assign bit_extender_2_out = {{20{immS[11]}}, immS};  // Bit_Extender bit_extender_2
  assign bit_extender_3_out = {{19{immB[12]}}, immB};  // Bit_Extender bit_extender_3
  assign bit_extender_4_out = {{11{immJ[20]}}, immJ};  // Bit_Extender bit_extender_4
  assign and_1_out = bit_extender_1_out & {32{1'b1}};  // AND_Gate and_1, 32 bits wide
  assign and_2_out = bit_extender_2_out & {32{1'b1}};  // AND_Gate and_2, 32 bits wide
  assign and_3_out = bit_extender_3_out & {32{1'b1}};  // AND_Gate and_3, 32 bits wide
  assign and_4_out = bit_extender_4_out & {32{1'b1}};  // AND_Gate and_4, 32 bits wide
  Multiplexer #(.width(32), .enable("false")) multiplexer_1 (
    .in0(bit_extender_1_out), .in1(and_1_out), .out(I), .sel(bitselector_1_out));
  Multiplexer #(.width(32), .enable("false")) multiplexer_2 (
    .in0(bit_extender_2_out), .in1(and_2_out), .out(S), .sel(bitselector_2_out));
  Multiplexer #(.width(32), .enable("false")) multiplexer_3 (
    .in0(bit_extender_3_out), .in1(and_3_out), .out(B), .sel(bitselector_3_out));
  Multiplexer #(.width(32), .enable("false")) multiplexer_4 (
    .in0(bit_extender_4_out), .in1(and_4_out), .out(J), .sel(bitselector_4_out));
  Multiplexer #(.select(3), .width(32), .enable("false")) multiplexer_5 (
    .in0(I), .in1(S), .in2(B), .in3(immU), .in4(J), .out(imm), .sel(ImmSel));  // open: in5, in6, in7

  // Other names for the same wires on the sheet: inst[31:0] = Instruction
endmodule

module Decodery (
  input  [31:0] Instruction,
  output [6:0] opcode,
  output [4:0] rd,
  output [4:0] rs1,
  output [4:0] rs2,
  output [2:0] funct3,
  output [6:0] funct7,
  output [11:0] immI,
  output [11:0] immS,
  output [12:0] immB,
  output [31:0] immU,
  output [20:0] immJ
);


  assign funct3 = Instruction[14:12];
  assign funct7 = Instruction[31:25];
  assign immB = {Instruction[31], Instruction[7], Instruction[30:25], Instruction[11:8], 1'b0};
  assign immI = Instruction[31:20];
  assign immJ = {Instruction[31], Instruction[19:12], Instruction[20], Instruction[30:21], 1'b0};
  assign immS = {Instruction[31:25], Instruction[11:7]};
  assign immU = {Instruction[31:12], {12{1'b0}}};
  assign opcode = Instruction[6:0];
  assign rd = Instruction[11:7];
  assign rs1 = Instruction[19:15];
  assign rs2 = Instruction[24:20];

  // Other names for the same wires on the sheet: inst[31:0] = Instruction
endmodule

module Control (
  input  [31:0] Instruction,
  input  BrEq,
  input  BrLt,
  output PCSel,
  output RegWEn,
  output [2:0] ImmSel,
  output BrUn,
  output BSel,
  output ASel,
  output [3:0] ALUSel,
  output MemRW,
  output [1:0] WBSel
);

  wire [2:0] funct3;
  wire [6:0] funct7, opcode;

  Decodery decodery_1 (
    .Instruction(Instruction), .opcode(opcode), .funct3(funct3), .funct7(funct7));  // open: rd, rs1, rs2, immI, immS, immB, immU, immJ

  // Other names for the same wires on the sheet: inst[31:0] = Instruction
endmodule

module BrCmp (
  input  [31:0] rs1,
  input  [31:0] rs2,
  input  BrUn,
  output BrEq,
  output BrLt
);

  wire comparator_1_eq, comparator_1_lt, comparator_2_eq, comparator_2_lt;

  Comparator #(.width(32)) comparator_1 (.a(rs1), .b(rs2), .eq(comparator_1_eq), .lt(comparator_1_lt));  // open: gt
  Comparator #(.width(32), .mode("unsigned")) comparator_2 (
    .a(rs1), .b(rs2), .eq(comparator_2_eq), .lt(comparator_2_lt));  // open: gt
  Multiplexer #(.enable("false")) multiplexer_1 (.in0(comparator_1_eq), .in1(comparator_2_eq), .out(BrEq), .sel(BrUn));
  Multiplexer #(.enable("false")) multiplexer_2 (.in0(comparator_1_lt), .in1(comparator_2_lt), .out(BrLt), .sel(BrUn));

  // Other names for the same wires on the sheet: A[31:0] = rs1; B[31:0] = rs2; isUnsigned = BrUn
endmodule
